# Fritzing sketch TikiBirds (saved by Fritzing 0.9.4)
breadboards: 1

parts:
  Raspberry_Pi_1 = Raspberry Pi 4 [part_number=RPI-4-b]
  U1 = RELAY-SOLIDSTATE [package=relay-s108t02]
  U2 = Module 4 Relais 5V [package="Module 4 Relais 5V"]
  U3 = Module 4 Relais 5V [package="Module 4 Relais 5V"]
  U4 = RELAY-SOLIDSTATE [package=relay-s108t02]
  U5 = RELAY-SOLIDSTATE [package=relay-s108t02]
  Part1 = LilyPad LED
  Part2 = LilyPad LED
  Part3 = LilyPad LED
  Part4 = LilyPad LED
  U6 = RELAY-SOLIDSTATE [package=relay-s108t02]
  VCC1 = 4 x AAA Battery Mount
  J1 = Power Jack [package=power_jack_slot]
  M1 = DC Motor
  M2 = DC Motor
  M3 = DC Motor
  M4 = DC Motor
  M5 = DC Motor
  M6 = DC Motor
  M7 = DC Motor
  M8 = DC Motor
  M9 = fc-51 [package=THT]

nets:
  N1: Raspberry_Pi_1.GPIO4, M9.pin1
  N2: Raspberry_Pi_1.GPIO17, U5.+
  N3: Raspberry_Pi_1.GPIO27, U3.IN2
  N4: Raspberry_Pi_1.GPIO22, U4.+
  N5: Raspberry_Pi_1.GPIO5, U3.IN1
  N6: Raspberry_Pi_1.GPIO6, U3.IN4
  N7: Raspberry_Pi_1.GPIO13, U3.IN3
  N8: Raspberry_Pi_1.GPIO19, U1.+
  N9: Raspberry_Pi_1.GPIO26, U2.IN3
  GND: Raspberry_Pi_1.GND, U1.-, U2.GND, U3.GND, U4.-, U5.-, U6.-, M9.pin2
  N10: Raspberry_Pi_1.GPIO21, U2.IN2
  N11: Raspberry_Pi_1.GPIO20, U6.+
  N12: Raspberry_Pi_1.GPIO24, U2.IN4
  N13: Raspberry_Pi_1.GPIO23, U2.IN1
  VCC: Raspberry_Pi_1.5V, U2.VCC, U3.VCC, M9.pin3
  N14: U1.T1, M5.pin_1
  N15: U1.T2, U2.K2-NO, U2.K4-NO, U3.K2-NO, U3.K4-NO, U4.T2, U5.T2, U6.T2, VCC1.-
  N16: U2.K1-NF, Part4.+
  N17: U2.K2-NF, M3.pin_2
  N18: U2.K3-NF, Part3.+
  N19: U2.K4-NF, M4.pin_2
  N20: U2.K1-NO, U2.K3-NO, U3.K1-NO, U3.K3-NO, J1.PWR
  N21: U3.K1-NF, Part2.+
  N22: U3.K2-NF, M2.pin_2
  N23: U3.K3-NF, Part1.+
  N24: U3.K4-NF, M1.pin_2
  N25: U4.T1, M7.pin_1
  N26: U5.T1, M8.pin_1
  N27: Part1.-, Part2.-, Part3.-, Part4.-, J1.GND
  N28: U6.T1, M6.pin_1
  N29: VCC1.+, M5.pin_2, M6.pin_2, M7.pin_2, M8.pin_2

notes:
  Body
  Beak
  Lights
  Solid State Relay
  Separate power for lights
  IR Motion Sensor
  6V power

custom parts:
  Raspberry Pi 4: The RPi4, a faster version of the awesome Raspberry Pi 2 B ARM Board with 40 pin gpio. Ready for special Raspberry Pi B+ and RPi2 Hat (Hardware attached (on) top)
  Module 4 Relais 5V: Module 4 Relais 5V 4x SPD-06VDC-SD-C
