# Fritzing sketch TikiBirds_v3.2 (saved by Fritzing 0.9.4)
circuit board: 6.80863cm x 17.4839cm

parts:
  Part1 = LilyPad LED
  Part2 = LilyPad LED
  Part3 = LilyPad LED
  Part4 = LilyPad LED
  VCC1 = 4 x AAA Battery Mount
  J1 = Power Jack [package=power_jack_slot]
  M5 = DC Motor
  M12 = DC Motor
  M13 = DC Motor
  M14 = DC Motor
  M15 = DC Motor
  Raspberry_Pi1 = Raspberry Pi B+
  M8 = DC Motor
  Part5 = 2 Channel SSR
  Part6 = 2 Channel SSR
  Part7 = 2 Channel SSR
  Part8 = 2 Channel SSR
  U1 = Module 4 Relais 5V [package="Module 4 Relais 5V"]
  M7 = DC Motor
  M18 = DC Motor
  SP1 = SPEAKER [package=pcb_mount_speaker]
  SP2 = SPEAKER [package=pcb_mount_speaker]
  SP3 = SPEAKER [package=pcb_mount_speaker]
  SP4 = SPEAKER [package=pcb_mount_speaker]
  AMP1 = PAM8403 6W Stereo Amplifier
  AMP2 = PAM8403 6W Stereo Amplifier
  AMP3 = PAM8403 6W Stereo Amplifier
  RY1 = SSR-40VA
  SP5 = SPEAKER [package=pcb_mount_speaker]
  SP6 = SPEAKER [package=pcb_mount_speaker]

nets:
  N1: Part1.+, U1.K1-NO
  N2: Part1.-, Part2.-, Part3.-, Part4.-, J1.GND
  N3: Part2.+, U1.K2-NO
  N4: Part3.+, U1.K3-NO
  N5: Part4.+, U1.K4-NO
  N6: VCC1.-, Part5.COM1, Part5.NO2, Part6.COM1, Part6.NO2, Part7.COM1, Part7.NO2, Part8.COM1, Part8.NO2
  N7: VCC1.+, M5.pin_2, M12.pin_2, M13.pin_2, M14.pin_2, M15.pin_2, M8.pin_2, M7.pin_2, M18.pin_2
  N8: J1.PWR, U1.K1-NF, U1.K2-NF, U1.K3-NF, U1.K4-NF
  N9: M5.pin_1, Part7.COM2
  N10: M12.pin_1, Part8.NO1
  N11: M13.pin_1, Part7.NO1
  N12: M14.pin_1, Part6.NO1
  N13: M15.pin_1, Part5.NO1
  N14: Raspberry_Pi1.GPIO17, Part8.X1
  N15: Raspberry_Pi1.GPIO27, Part8.X2
  N16: Raspberry_Pi1.GPIO22, Part7.X1
  N17: Raspberry_Pi1.GPIO6, Part6.X1
  N18: Raspberry_Pi1.GPIO13, U1.IN4
  N19: Raspberry_Pi1.GPIO19, Part6.X2
  N20: Raspberry_Pi1.GPIO26, RY1.Pin_4
  GND: Raspberry_Pi1.GND, Part5.DC-, Part5.XM, Part6.DC-, Part6.XM, Part7.DC-, Part7.XM, Part8.DC-, Part8.XM, U1.GND, U1.IN3, AMP1.Ground#3, AMP2.Ground#3, AMP3.Ground, RY1.Pin_3
  N21: Raspberry_Pi1.GPIO21, Part5.X2
  N22: Raspberry_Pi1.GPIO20, Part5.X1
  N23: Raspberry_Pi1.GPIO24, Part7.X2
  N24: Raspberry_Pi1.GPIO23, U1.IN2
  5V: Raspberry_Pi1.5V, Part5.DC+, Part6.DC+, Part7.DC+, Part8.DC+, U1.VCC, RY1.Pin_1
  N25: M8.pin_1, Part6.COM2
  N26: Part5.COM2, M7.pin_1
  N27: Part8.COM2, M18.pin_1
  N28: SP1.+, AMP1.L_Out_-
  N29: SP1.-, AMP1.L_Out_+
  N30: SP2.+, AMP2.R_Out_-
  N31: SP2.-, AMP2.R_Out_+
  N32: SP3.+, AMP1.R_Out_-
  N33: SP3.-, AMP1.R_Out_+
  N34: SP4.+, AMP2.L_Out_-
  N35: SP4.-, AMP2.L_Out_+
  5V_2: AMP1.5V, AMP2.5V, AMP3.5V, RY1.Pin_2
  N36: AMP3.L_Out_-, SP5.+
  N37: AMP3.L_Out_+, SP5.-
  N38: AMP3.R_Out_-, SP6.+
  N39: AMP3.R_Out_+, SP6.-

notes:
  6V power
  Light Power
  Michael
  Fritz
  Pierre
  Jose
  Amplifiers with 3.5mm jack (not actual part)

custom parts:
  Module 4 Relais 5V: Module 4 Relais 5V 4x SPD-06VDC-SD-C
  PAM8403 6W Stereo Amplifier: PAM8403 6 Watt Stereo Amplifier
  SSR-40VA: SSR-40VA solid state relay.
