# Fritzing sketch TikiBirds_v3 (saved by Fritzing 0.9.4)
circuit board: 6.80863cm x 17.4839cm
breadboards: 1

parts:
  Part1 = LilyPad LED
  Part2 = LilyPad LED
  Part3 = LilyPad LED
  Part4 = LilyPad LED
  VCC1 = 4 x AAA Battery Mount
  J1 = Power Jack [package=power_jack_slot]
  M5 = DC Motor
  M6 = DC Motor
  M7 = DC Motor
  M9 = fc-51 [package=THT]
  M12 = DC Motor
  M13 = DC Motor
  M14 = DC Motor
  M15 = DC Motor
  Raspberry_Pi1 = Raspberry Pi B+
  M8 = DC Motor
  Part5 = 2 Channel SSR
  Part6 = 2 Channel SSR
  Part7 = 2 Channel SSR
  Part8 = 2 Channel SSR
  U1 = Module 4 Relais 5V [package="Module 4 Relais 5V"]

nets:
  N1: Part1.+, U1.K1-NO
  N2: Part1.-, Part2.-, Part3.-, Part4.-, J1.GND
  N3: Part2.+, U1.K2-NO
  N4: Part3.+, U1.K3-NO
  N5: Part4.+, U1.K4-NO
  N6: VCC1.-, Part5.COM1, Part5.COM2, Part6.COM1, Part6.COM2, Part7.COM1, Part7.COM2, Part8.COM1, Part8.COM2
  N7: VCC1.+, M5.pin_2, M6.pin_2, M7.pin_2, M12.pin_2, M13.pin_2, M14.pin_2, M15.pin_2, M8.pin_2
  N8: J1.PWR, U1.K1-NF, U1.K2-NF, U1.K3-NF, U1.K4-NF
  N9: M5.pin_1, Part7.NO2
  N10: M6.pin_1, Part8.NO2
  N11: M7.pin_1, Part5.NO2
  N12: M9.pin1, Raspberry_Pi1.GPIO3
  GND: M9.pin2, Raspberry_Pi1.GND, Part5.DC-, Part5.XM, Part5.X1, Part6.DC-, Part6.XM, Part7.DC-, Part7.XM, Part8.DC-, Part8.XM, U1.GND, U1.IN1
  5V: M9.pin3, Raspberry_Pi1.5V, Part5.DC+, Part6.DC+, Part7.DC+, Part8.DC+, U1.VCC
  N13: M12.pin_1, Part8.NO1
  N14: M13.pin_1, Part7.NO1
  N15: M14.pin_1, Part6.NO1
  N16: M15.pin_1, Part5.NO1
  N17: Raspberry_Pi1.GPIO17, Part7.X2
  N18: Raspberry_Pi1.GPIO27, Part6.X1
  N19: Raspberry_Pi1.ID_SD, U1.IN3
  N20: Raspberry_Pi1.GPIO5, Part8.X2
  N21: Raspberry_Pi1.GPIO6, U1.IN4
  N22: Raspberry_Pi1.GPIO13, Part7.X1
  N23: Raspberry_Pi1.GPIO19, U1.IN2
  N24: Raspberry_Pi1.GPIO20, Part5.X2
  N25: Raspberry_Pi1.GPIO16, Part8.X1
  N26: Raspberry_Pi1.GPIO23, Part6.X2
  N27: M8.pin_1, Part6.NO2

notes:
  Body
  Beaks
  Lights
  Relay for the lights
  Solid State Relayfor beaks & body
  Separate power for lights
  IR Motion Sensor
  6V power

custom parts:
  Module 4 Relais 5V: Module 4 Relais 5V 4x SPD-06VDC-SD-C
